// Logisim project CPU.circ as structural Verilog: 8 circuits, main circuit CPU
module CPU (
);

  wire ccr_1_c, ccr_1_i_2, ccr_1_n, ccr_1_z, clock_1_out, RESET_out, undriven, undriven_2, undriven_3,
       undriven_4, undriven_5, undriven_6, undriven_8, undriven_9, undriven_10, undriven_11, undriven_12,
       undriven_13, undriven_14, undriven_15, undriven_16;
  wire [3:0] undriven_7;
  wire [7:0] AX_probe_out, BX_probe_out, ram_1_d_o, SP_probe_out, undriven_17, Z_probe_out;

  CU cu_1 (.IN(ram_1_d_o), .CLOCK(clock_1_out), .RESET(RESET_out));  // open: PROBE_OP, SET_OP, out_6
  RAM ram_1 (
    .D_I(ram_1_d_o), .D_O(ram_1_d_o), .CLK(clock_1_out), .RST(RESET_out), .AR_I(undriven_4), .R(undriven),
    .W(undriven_2), .DR_I(undriven_3), .DR_O(undriven_5));
  CCR ccr_1 (.CF_I(undriven_8), .I(undriven_17), .C(ccr_1_c), .Z(ccr_1_z), .N(ccr_1_n), .I_2(ccr_1_i_2));  // open: IF_I
  ALU alu_1 (.C_O(undriven_8), .Z(undriven_17), .X(ram_1_d_o), .Y(AX_probe_out), .C_I(undriven_6), .OP(undriven_7));
  Clock clock_1 (.out(clock_1_out));
  Button RESET (.out(RESET_out));
  // Probe on ram_1_d_o
  REGISTER AX (
    .I(ram_1_d_o), .R_I(undriven_9), .R_O(undriven_10), .CLK(clock_1_out), .RST(RESET_out), .O(ram_1_d_o),
    .PROBE_OUT(AX_probe_out));
  // Probe on AX_probe_out
  REGISTER BX (
    .I(ram_1_d_o), .R_I(undriven_11), .R_O(undriven_12), .CLK(clock_1_out), .RST(RESET_out), .O(ram_1_d_o),
    .PROBE_OUT(BX_probe_out));
  // Probe on BX_probe_out
  REGISTER SP (
    .I(ram_1_d_o), .R_I(undriven_13), .R_O(undriven_14), .CLK(clock_1_out), .RST(RESET_out), .O(ram_1_d_o),
    .PROBE_OUT(SP_probe_out));
  // Probe on SP_probe_out
  REGISTER Z (
    .I(undriven_17), .R_I(undriven_15), .R_O(undriven_16), .CLK(clock_1_out), .RST(RESET_out),
    .PROBE_OUT(Z_probe_out));  // open: O
  // Probe on Z_probe_out

  // Notes on the sheet:
  //   CPU
endmodule

module CU (
  input  [7:0] IN,
  input  CLOCK,
  input  RESET,
  input  SET_OP,
  output [7:0] PROBE_OP,
  output [23:0] out_6
);

  wire comparator_1_eq, comparator_2_eq, not_1_out, not_2_out, not_3_out, or_1_out, or_2_out;
  wire [7:0] controlled_buffer_1_out, counter_1_q;
  wire [23:0] rom_1_data;

  assign controlled_buffer_1_out = SET_OP ? IN : 8'bz;  // Controlled_Buffer controlled_buffer_1
  not not_1 (not_1_out, CLOCK);
  Register OP (.D(controlled_buffer_1_out), .en(SET_OP), .Q(PROBE_OP), .clk(CLOCK), .clr(RESET));
  Counter counter_1 (
    .load(comparator_1_eq), .D(PROBE_OP), .count(not_2_out), .Q(counter_1_q), .clk(not_1_out), .clr(or_1_out));  // open: carry
  or or_1 (or_1_out, RESET, comparator_2_eq);
  not not_2 (not_2_out, comparator_1_eq);
  ROM #(.dataWidth(24)) rom_1 (.addr(counter_1_q), .data(rom_1_data), .sel(1'b1));
  Comparator #(.width(24)) comparator_1 (.a(rom_1_data), .b({24{1'b1}}), .eq(comparator_1_eq));  // open: gt, lt
  Comparator #(.width(24)) comparator_2 (.a(rom_1_data), .b({24{1'b0}}), .eq(comparator_2_eq));  // open: gt, lt
  Pull_Resistor pull_resistor_1 (.node(out_6));
  assign out_6 = not_3_out ? rom_1_data : 24'bz;  // Controlled_Buffer controlled_buffer_2
  not not_3 (not_3_out, or_2_out);
  or or_2 (or_2_out, comparator_1_eq, comparator_2_eq);

  // Notes on the sheet:
  //   CONTROL UNIT
  //   JUMP TO OP
  //   RESET COUNTER
  //   contents of rom_1 (hex, n*v repeats v):
  //   400040 800080 280000 46000 400040 800080 282000 ffffff 40001
endmodule

module RAM (
  input  CLK,
  input  RST,
  input  AR_I,
  input  R,
  input  W,
  input  DR_I,
  input  DR_O,
  input  [7:0] D_I,
  output [7:0] D_O
);

  wire not_1_out, or_1_out;
  wire [7:0] AR_2_o, AR_2_probe_out, controlled_buffer_2_out, DR_o_2, DR_probe_out, ram_1_data;

  // Probe on AR_2_probe_out
  REGISTER AR_2 (.I(D_I), .R_I(AR_I), .R_O(1'b1), .CLK(CLK), .RST(RST), .O(AR_2_o), .PROBE_OUT(AR_2_probe_out));
  or or_1 (or_1_out, W, R);
  RAM_part ram_1 (.addr(AR_2_o), .data(ram_1_data), .sel(or_1_out), .clk(CLK), .ld(R), .clr(RST));
  assign ram_1_data = W ? DR_o_2 : 8'bz;  // Controlled_Buffer controlled_buffer_1
  assign controlled_buffer_2_out = R ? ram_1_data : 8'bz;  // Controlled_Buffer controlled_buffer_2
  REGISTER DR (
    .I(controlled_buffer_2_out), .R_I(DR_I), .R_O(DR_O), .CLK(CLK), .RST(RST), .O(DR_o_2),
    .PROBE_OUT(DR_probe_out));
  // Probe on DR_probe_out
  not not_1 (not_1_out, R);
  assign controlled_buffer_2_out = not_1_out ? D_I : 8'bz;  // Controlled_Buffer controlled_buffer_3
  assign D_O = R ? DR_o_2 : 8'bz;  // Controlled_Buffer controlled_buffer_4

  // Notes on the sheet:
  //   RANDOM ACCESS MEMORY
  //   RAM
endmodule

module REGISTER (
  input  [7:0] I,
  input  R_I,
  input  R_O,
  input  CLK,
  input  RST,
  output [7:0] O,
  output [7:0] PROBE_OUT
);

  wire [7:0] controlled_buffer_1_out;

  Register R (.D(controlled_buffer_1_out), .Q(PROBE_OUT), .clk(CLK), .clr(RST));  // open: en
  assign controlled_buffer_1_out = R_I ? I : 8'bz;  // Controlled_Buffer controlled_buffer_1
  assign O = R_O ? PROBE_OUT : 8'bz;  // Controlled_Buffer controlled_buffer_2

  // Notes on the sheet:
  //   8BIT REGISTER
endmodule

module ALU (
  input  [7:0] X,
  input  [7:0] Y,
  input  C_I,
  input  [3:0] OP,
  input  C_O,
  input  [7:0] Z
);

  wire and_2_out;
  wire [7:0] and_1_out, fulladder_8bit_1_z, or_1_out, shifter_1_out, shifter_2_out, shifter_3_out,
       shifter_4_out, shifter_5_out, xor_1_out;

  FULLADDER_8BIT fulladder_8bit_1 (.X(X), .Y(Y), .SUB(and_2_out), .C_I(C_I), .Z(fulladder_8bit_1_z), .C_O(C_O));
  assign and_1_out = X & Y;  // AND_Gate and_1, 8 bits wide
  assign or_1_out = X | Y;  // OR_Gate or_1, 8 bits wide
  assign xor_1_out = X ^ Y;  // XOR_Gate xor_1, 8 bits wide
  Shifter shifter_1 (.in(X), .\dist (3'b001), .out(shifter_1_out));
  Shifter #(.shift("lr")) shifter_2 (.in(X), .\dist (3'b001), .out(shifter_2_out));
  Shifter #(.shift("ar")) shifter_3 (.in(X), .\dist (3'b001), .out(shifter_3_out));
  Shifter #(.shift("rl")) shifter_4 (.in(X), .\dist (3'b001), .out(shifter_4_out));
  Shifter #(.shift("rr")) shifter_5 (.in(X), .\dist (3'b001), .out(shifter_5_out));
  and and_2 (and_2_out, OP[0], ~OP[1], ~OP[2], ~OP[3]);  // AND_Gate
  Multiplexer #(.select(4), .width(8), .disabled(0), .enable("false")) multiplexer_1 (
    .in0(fulladder_8bit_1_z), .in1(fulladder_8bit_1_z), .in2(and_1_out), .in3(or_1_out), .in4(xor_1_out),
    .in5(shifter_1_out), .in6(shifter_2_out), .in7(shifter_3_out), .in8(shifter_4_out), .in9(shifter_5_out),
    .out(Z), .sel(OP));  // open: in10, in11, in12, in13, in14, in15

  // Notes on the sheet:
  //   ALU
endmodule

module FULLADDER_8BIT (
  input  [7:0] X,
  input  [7:0] Y,
  input  SUB,
  input  C_I,
  output [7:0] Z,
  output C_O
);

  wire fulladder_1bit_1_c_o, fulladder_1bit_2_c_o, fulladder_1bit_3_c_o, fulladder_1bit_4_c_o,
       fulladder_1bit_5_c_o, fulladder_1bit_6_c_o, fulladder_1bit_7_c_o, or_1_out, xor_1_out, xor_2_out,
       xor_3_out, xor_4_out, xor_5_out, xor_6_out, xor_7_out, xor_8_out;

  or or_1 (or_1_out, SUB, C_I);
  xor xor_1 (xor_1_out, SUB, Y[0]);
  xor xor_2 (xor_2_out, SUB, Y[1]);
  xor xor_3 (xor_3_out, SUB, Y[2]);
  xor xor_4 (xor_4_out, SUB, Y[3]);
  xor xor_5 (xor_5_out, SUB, Y[4]);
  xor xor_6 (xor_6_out, SUB, Y[5]);
  xor xor_7 (xor_7_out, SUB, Y[6]);
  xor xor_8 (xor_8_out, SUB, Y[7]);
  FULLADDER_1BIT fulladder_1bit_1 (.X(X[0]), .Y(xor_1_out), .C_I(or_1_out), .C_O(fulladder_1bit_1_c_o), .Z(Z[0]));
  FULLADDER_1BIT fulladder_1bit_2 (
    .X(X[1]), .Y(xor_2_out), .C_I(fulladder_1bit_1_c_o), .C_O(fulladder_1bit_2_c_o), .Z(Z[1]));
  FULLADDER_1BIT fulladder_1bit_3 (
    .X(X[2]), .Y(xor_3_out), .C_I(fulladder_1bit_2_c_o), .C_O(fulladder_1bit_3_c_o), .Z(Z[2]));
  FULLADDER_1BIT fulladder_1bit_4 (
    .X(X[3]), .Y(xor_4_out), .C_I(fulladder_1bit_3_c_o), .C_O(fulladder_1bit_4_c_o), .Z(Z[3]));
  FULLADDER_1BIT fulladder_1bit_5 (
    .X(X[4]), .Y(xor_5_out), .C_I(fulladder_1bit_4_c_o), .C_O(fulladder_1bit_5_c_o), .Z(Z[4]));
  FULLADDER_1BIT fulladder_1bit_6 (
    .X(X[5]), .Y(xor_6_out), .C_I(fulladder_1bit_5_c_o), .C_O(fulladder_1bit_6_c_o), .Z(Z[5]));
  FULLADDER_1BIT fulladder_1bit_7 (
    .X(X[6]), .Y(xor_7_out), .C_I(fulladder_1bit_6_c_o), .C_O(fulladder_1bit_7_c_o), .Z(Z[6]));
  FULLADDER_1BIT fulladder_1bit_8 (.X(X[7]), .Y(xor_8_out), .C_I(fulladder_1bit_7_c_o), .C_O(C_O), .Z(Z[7]));

  // Notes on the sheet:
  //   FULL ADDER 8BIT
endmodule

module FULLADDER_1BIT (
  input  X,
  input  Y,
  input  C_I,
  output C_O,
  output Z
);

  wire and_1_out, and_2_out, xor_1_out;

  and and_1 (and_1_out, X, Y);
  xor xor_1 (xor_1_out, X, Y);
  or or_1 (C_O, and_1_out, and_2_out);
  and and_2 (and_2_out, xor_1_out, C_I);
  xor xor_2 (Z, xor_1_out, C_I);

  // Notes on the sheet:
  //   FULL ADDER 1BIT
endmodule

module CCR (
  input  CF_I,
  input  [7:0] I,
  input  IF_I,
  output C,
  output Z,
  output N,
  output I_2
);

  Comparator comparator_1 (.a(I), .b({8{1'b0}}), .eq(Z));  // open: gt, lt

  assign C = CF_I;
  assign I_2 = IF_I;
  assign N = I[7];

  // Notes on the sheet:
  //   CONDITION CODE REGISTER
endmodule
